// Logisim project sprout8.circ as structural Verilog: 2 circuits, main circuit main
module main (
);

  pc pc_1 ();  // open: d, load, inc, clk, rst, q
endmodule

module pc (
  input  [7:0] d,
  input  load,
  input  inc,
  input  clk,
  input  rst,
  output [7:0] q
);

  wire or_1_out;
  wire [7:0] adder_1_out, multiplexer_1_out;

  Multiplexer #(.width(8)) multiplexer_1 (.in0(adder_1_out), .in1(d), .out(multiplexer_1_out), .sel(load));
  or or_1 (or_1_out, load, inc);
  Register register_1 (.D(multiplexer_1_out), .en(or_1_out), .clk(clk), .Q(q), .clr(rst));
  Adder adder_1 (.a(8'h1), .b(q), .out(adder_1_out));  // open: cin, cout

  // Notes on the sheet:
  //   PROGRAM COUNTER CIRCUIT
endmodule
